# Fritzing sketch Dht11 (saved by Fritzing 0.9.3b)
breadboards: 1

parts:
  U1 = NodeMCU V1.0
  R1 = Resistor [tolerance=±5% resistance=220 package=THT]
  RHT1 = Humidity and Temperature Sensor RHT03
  LED1 = LED - 3mm [color="Red (633nm)" package="3 mm [THT]"]
  LED2 = LED - 3mm [color="Green (555nm)" package="3 mm [THT]"]
  LED3 = LED - 3mm [color="Blue (430nm)" package="3 mm [THT]"]

nets:
  N1: U1.D0, LED1.anode
  N2: U1.D2, LED2.anode
  N3: U1.D3, LED3.anode
  N4: U1.GND, RHT1.GND_2, LED1.cathode, LED2.cathode, LED3.cathode
  N5: U1.D5, R1.Pin_1
  VIN: U1.Vin, RHT1.Vcc
  N6: R1.Pin_0, RHT1.Data-signal

custom parts:
  NodeMCU V1.0: ESP8266 based NodeMCU
